# Fritzing sketch barcode_logger_arduino_nano_sample (saved by Fritzing 0.8.5b)
circuit board: 6.88566cm x 5.36311cm
breadboards: 1

parts:
  microSD_card_module_3_3V = microSD Socket [package="Molex 502774-0891 [SMD]"]
  RTC_DS1307 = Real Time Clock Module - DS1307 RTC Breakout Board
  Bluetooth_3_3V = Bluetooth Module Breakout - Roving Networks (RN-41)
  Li-Ion_battery_pack_6-7_4V = Battery
  R2 = Resistor [tolerance=±5% resistance=2.2k package=THT]
  R3 = Resistor [tolerance=±5% resistance=1k package=THT]
  C1 = Tantalum Capacitor [capacitance=100nF package="100 mil [THT, tantalum]"]
  Часть1 = Arduino Nano (Rev3.0)
  Arduino_Nano = Arduino Nano (Rev3.0)
  U1 = mini DIN 6 Connector [package=mini-din6]

nets:
  N1: microSD_card_module_3_3V.CS, Часть1.D10, Arduino_Nano.D10
  N2: microSD_card_module_3_3V.DI, Часть1.D11/MOSI, Arduino_Nano.D11/MOSI
  5V: microSD_card_module_3_3V.VCC, RTC_DS1307.5V, Часть1.5V, Arduino_Nano.5V, U1.4
  N3: microSD_card_module_3_3V.SCK, Часть1.D13/SCK, Arduino_Nano.D13/SCK
  N4: microSD_card_module_3_3V.GND, U1.3
  N5: microSD_card_module_3_3V.DO, Часть1.D12/MISO, Arduino_Nano.D12/MISO
  GND: RTC_DS1307.GND, Bluetooth_3_3V.GND, Li-Ion_battery_pack_6-7_4V.-, R2.Pin_1, C1.-, Часть1.GND, Arduino_Nano.GND
  N6: RTC_DS1307.SCL, Часть1.A5, Arduino_Nano.A5
  N7: RTC_DS1307.SDA, Часть1.A4, Arduino_Nano.A4
  3V3: Bluetooth_3_3V.VCC, C1.+, Часть1.3V3, Arduino_Nano.3V3
  N8: Bluetooth_3_3V.UARTRX, Часть1.D1/TX, Arduino_Nano.D1/TX
  VIN: Li-Ion_battery_pack_6-7_4V.+, Часть1.VIN, Arduino_Nano.VIN
  N9: R3.Pin_0, Часть1.D0/RX, Arduino_Nano.D0/RX
  N10: Часть1.RESET, Arduino_Nano.RESET
  N11: Часть1.D2, Arduino_Nano.D2
  N12: Часть1.D3, Arduino_Nano.D3, U1.5
  N13: Часть1.D4, Arduino_Nano.D4, U1.1
  N14: Часть1.D5, Arduino_Nano.D5
  N15: Часть1.D6, Arduino_Nano.D6
  N16: Часть1.D7, Arduino_Nano.D7
  N17: Часть1.D8, Arduino_Nano.D8
  N18: Часть1.D9, Arduino_Nano.D9
  N19: Часть1.A7, Arduino_Nano.A7
  N20: Часть1.A6, Arduino_Nano.A6
  N21: Часть1.A3, Arduino_Nano.A3
  N22: Часть1.A2, Arduino_Nano.A2
  N23: Часть1.A1, Arduino_Nano.A1
  N24: Часть1.A0, Arduino_Nano.A0
  N25: Часть1.AREF, Arduino_Nano.AREF

custom parts:
  Battery: Your standard 2x AA battery pack (3 Volts)
